// Digital circuit 4bit_ALU_Sana.dig as structural Verilog
module _4bit_ALU_Sana (
  input  [3:0] A,
  input  [3:0] B,
  input  [2:0] Control,
  input  Cin,
  input  [3:0] in_8,
  input  [3:0] in_9,
  output [3:0] Output,
  output Zero_flag,
  output Cout,
  output slt_flag
);

  wire _4bit_full_adder_sana_1_cout;
  wire [3:0] _4bit_full_adder_sana_1_sum, _4bit_subtractor_sana_1_subtraction, and_1_out, or_1_out, xor_1_out;

  _4bit_full_Adder_sana _4bit_full_adder_sana_1 (
    .A(A), .B(B), .Cin(Cin), .Sum(_4bit_full_adder_sana_1_sum), .Cout(_4bit_full_adder_sana_1_cout));
  _4bit_subtractor_sana _4bit_subtractor_sana_1 (
    .A(A), .B(B), .C(_4bit_full_adder_sana_1_cout), .Subtraction(_4bit_subtractor_sana_1_subtraction),
    .Cout(Cout));
  assign and_1_out = A & B;  // And and_1, 4 bits wide
  assign or_1_out = A | B;  // Or or_1, 4 bits wide
  assign xor_1_out = A ^ B;  // XOr xor_1, 4 bits wide
  Multiplexer #(.Selector_Bits(3), .Bits(4)) multiplexer_1 (
    .sel(Control), .in_0(_4bit_full_adder_sana_1_sum), .in_1(_4bit_subtractor_sana_1_subtraction),
    .in_2(and_1_out), .in_3(or_1_out), .in_4(xor_1_out), .in_5(_4bit_subtractor_sana_1_subtraction),
    .in_6(in_8), .in_7(in_9), .out(Output));
  nor nor_1 (Zero_flag, Output[0], Output[1], Output[2], Output[3]);

  assign slt_flag = Output[3];
endmodule
